// Logisim project Archi.circ as structural Verilog
module Additioneur_4bits (
  input  [3:0] A,
  input  [3:0] B,
  input  in_3,
  output [3:0] S,
  output Super_P,
  output Super_G
);

  wire add_1_g, add_1_p, add_2_g, add_2_p, add_3_g, add_3_p, add_4_g, add_4_p, anticipateur_1_c1,
       anticipateur_1_c2, anticipateur_1_c3;

  and and_1 (Super_P, add_1_p, add_2_p, add_3_p, add_4_p);
  Add add_1 (.A(B[0]), .Cin(in_3), .B(A[0]), .P(add_1_p), .G(add_1_g), .S(S[0]));
  Add add_2 (.A(B[1]), .Cin(anticipateur_1_c1), .B(A[1]), .P(add_2_p), .G(add_2_g), .S(S[1]));
  Anticipateur anticipateur_1 (
    .C0(in_3), .P1(add_1_p), .G1(add_1_g), .P2(add_2_p), .G2(add_2_g), .P3(add_3_p), .G3(add_3_g),
    .P4(add_4_p), .G4(add_4_g), .c1(anticipateur_1_c1), .c2(anticipateur_1_c2), .c3(anticipateur_1_c3),
    .c4(Super_G));
  Add add_3 (.A(B[2]), .Cin(anticipateur_1_c2), .B(A[2]), .P(add_3_p), .G(add_3_g), .S(S[2]));
  Add add_4 (.A(B[3]), .Cin(anticipateur_1_c3), .B(A[3]), .P(add_4_p), .G(add_4_g), .S(S[3]));
endmodule

module Add (
  input  A,
  input  Cin,
  input  B,
  output P,
  output G,
  output S
);

  wire xor_1_out;

  or or_1 (P, B, A);
  and and_1 (G, B, A);
  xor xor_1 (xor_1_out, A, B);
  xor xor_2 (S, xor_1_out, Cin);
endmodule

module additionneur_16bits (
  input  [15:0] A,
  input  [15:0] B,
  input  in_3,
  output Retenue,
  output [15:0] S
);

  wire additioneur_4bits_1_super_g, additioneur_4bits_1_super_p, additioneur_4bits_2_super_g,
       additioneur_4bits_2_super_p, additioneur_4bits_3_super_g, additioneur_4bits_3_super_p,
       additioneur_4bits_4_super_g, additioneur_4bits_4_super_p, anticipateur_1_c1, anticipateur_1_c2,
       anticipateur_1_c3;

  Additioneur_4bits additioneur_4bits_1 (
    .A(A[3:0]), .B(B[3:0]), .Super_P(additioneur_4bits_1_super_p), .S(S[3:0]),
    .Super_G(additioneur_4bits_1_super_g), .in_3(in_3));
  Anticipateur anticipateur_1 (
    .C0(in_3), .P1(additioneur_4bits_1_super_p), .G1(additioneur_4bits_1_super_g),
    .P2(additioneur_4bits_2_super_p), .G2(additioneur_4bits_2_super_g), .P3(additioneur_4bits_3_super_p),
    .G3(additioneur_4bits_3_super_g), .P4(additioneur_4bits_4_super_p), .G4(additioneur_4bits_4_super_g),
    .c1(anticipateur_1_c1), .c2(anticipateur_1_c2), .c3(anticipateur_1_c3), .c4(Retenue));
  Additioneur_4bits additioneur_4bits_2 (
    .A(A[7:4]), .B(B[7:4]), .Super_P(additioneur_4bits_2_super_p), .S(S[7:4]),
    .Super_G(additioneur_4bits_2_super_g), .in_3(anticipateur_1_c1));
  Additioneur_4bits additioneur_4bits_3 (
    .A(A[11:8]), .B(B[11:8]), .Super_P(additioneur_4bits_3_super_p), .S(S[11:8]),
    .Super_G(additioneur_4bits_3_super_g), .in_3(anticipateur_1_c2));
  Additioneur_4bits additioneur_4bits_4 (
    .A(A[15:12]), .B(B[15:12]), .Super_P(additioneur_4bits_4_super_p), .S(S[15:12]),
    .Super_G(additioneur_4bits_4_super_g), .in_3(anticipateur_1_c3));
endmodule

module Soustraction (
  input  [15:0] in_1,
  input  in_2,
  input  [15:0] in_3,
  output [15:0] out_4,
  output out_5
);

  wire [15:0] not_1_out;

  assign not_1_out = ~in_3;  // NOT_Gate not_1, 16 bits wide
  Adder #(.width(16)) adder_1 (.a(in_1), .b(not_1_out), .out(out_4), .cin(in_2), .cout(out_5));
endmodule

module UAL (
  input  [15:0] A,
  input  [15:0] B,
  input  [2:0] in_3,
  output [3:0] ZNCV,
  output [15:0] S
);

  wire adder_1_cout, Soustraction_out_5;
  wire [15:0] adder_1_out, and_1_out, not_1_out, or_1_out, shifter_1_out, shifter_2_out, Soustraction_out_4,
       xor_1_out;

  assign not_1_out = ~A;  // NOT_Gate not_1, 16 bits wide
  Adder #(.width(16)) adder_1 (.a(A), .b(B), .out(adder_1_out), .cin(1'b0), .cout(adder_1_cout));
  Soustraction Soustraction (.in_1(A), .in_3(B), .in_2(1'b1), .out_5(Soustraction_out_5), .out_4(Soustraction_out_4));
  assign and_1_out = A & B;  // AND_Gate and_1, 16 bits wide
  assign or_1_out = A | B;  // OR_Gate or_1, 16 bits wide
  assign xor_1_out = A ^ B;  // XOR_Gate xor_1, 16 bits wide
  Shifter #(.width(16)) shifter_1 (.in(A), .\dist (4'b0001), .out(shifter_1_out));
  Shifter #(.width(16), .shift("ar")) shifter_2 (.in(A), .\dist (4'b0001), .out(shifter_2_out));
  Multiplexer #(.select(3), .width(16), .enable("false")) multiplexer_1 (
    .in0(adder_1_out), .in1(Soustraction_out_4), .in2(not_1_out), .in3(and_1_out), .in4(or_1_out),
    .in5(xor_1_out), .in6(shifter_1_out), .in7(shifter_2_out), .out(S), .sel(in_3));
  nor nor_1 (ZNCV[3], S[0], S[1], S[2], S[3], S[4], S[5], S[6], S[7], S[8], S[9], S[10], S[11], S[12], S[13], S[14], S[15]);

  assign ZNCV[2] = S[15];
endmodule

module Anticipateur (
  input  C0,
  input  P1,
  input  G1,
  input  P2,
  input  G2,
  input  P3,
  input  G3,
  input  P4,
  input  G4,
  output c1,
  output c2,
  output c3,
  output c4
);

  wire and_1_out, and_2_out, and_3_out, and_4_out, and_5_out, and_6_out, and_7_out, and_8_out, and_9_out,
       and_10_out;

  and and_1 (and_1_out, P1, C0);
  and and_2 (and_2_out, C0, P1, P2, P3, P4);
  and and_3 (and_3_out, P4, P3, P2, G1);
  and and_4 (and_4_out, P4, P3, G2);
  and and_5 (and_5_out, P4, G3);
  or or_1 (c1, and_1_out, G1);
  and and_6 (and_6_out, C0, P1, P2);
  and and_7 (and_7_out, G1, P2);
  and and_8 (and_8_out, C0, P1, P2, P3);
  and and_9 (and_9_out, G1, P2, P3);
  and and_10 (and_10_out, P3, G2);
  or or_2 (c2, and_6_out, and_7_out, G2);
  or or_3 (c3, and_8_out, and_9_out, and_10_out, G3);
  or or_4 (c4, G4, and_2_out, and_3_out, and_4_out, and_5_out);
endmodule

module overflow (
  input  a,
  input  b,
  input  c,
  output x
);

  wire and_1_out, and_2_out, not_1_out, not_2_out, not_3_out;

  not not_1 (not_1_out, a);
  not not_2 (not_2_out, b);
  not not_3 (not_3_out, c);
  and and_1 (and_1_out, not_1_out, not_2_out, c);
  and and_2 (and_2_out, a, b, not_3_out);
  or or_1 (x, and_1_out, and_2_out);
endmodule

module Test (
  input  a,
  input  b,
  input  c,
  output x,
  output y,
  output z
);

  wire not_1_out, not_2_out;

  not not_1 (not_1_out, a);
  not not_2 (not_2_out, b);
  and and_1 (z, not_1_out, not_2_out, c);

  assign x = 1'b0;
  assign y = 1'b0;
endmodule
